# Fritzing sketch Umidade Solo e Ar Temp Ar (saved by Fritzing 0.9.3b)
circuit board: 7.69313cm x 6.71488cm
breadboards: 1

parts:
  부품1 = Arduino Uno (Rev3)
  R1 = Resistor [tolerance=±5% resistance=220 package=THT]
  R2 = Resistor [tolerance=±5% resistance=220 package=THT]
  LED1 = LED - 5mm [color="Red (633nm)" package="5 mm [THT]"]
  LED2 = LED - 5mm [color="Green (555nm)" package="5 mm [THT]"]
  LCM1602_IIC2 = LCM1602 IIC [part_number="LCM1602 IIC" chip_label="LCM1602 IIC" package="DIP (Dual Inline) [THT]"]
  LCD2 = LCD screen
  DHT1 = DHT11 Humitidy and Temperature Sensor
  J1 = female pin header, 4 pins [form="♀ (female)"]

nets:
  N1: 부품1.A0, J1.pin1
  N2: 부품1.A4/SDA, LCM1602_IIC2.SDA
  N3: 부품1.A5/SCL, LCM1602_IIC2.SCL
  N4: 부품1.D8, DHT1.DATA
  N5: 부품1.D3_PWM, LED1.anode
  N6: 부품1.D4, LED2.anode
  5V: 부품1.5V, LCM1602_IIC2.VCC, DHT1.VDD, J1.pin4
  GND: 부품1.GND, R1.Pin_1, R2.Pin_1, LCM1602_IIC2.GND, DHT1.GND, J1.pin3
  N7: R1.Pin_0, LED1.cathode
  N8: R2.Pin_0, LED2.cathode
  VSS: LCM1602_IIC2.VSS, LCD2.VSS
  VDD: LCM1602_IIC2.VDD, LCD2.VDD
  N9: LCM1602_IIC2.V0, LCD2.V0
  N10: LCM1602_IIC2.RS, LCD2.RS
  N11: LCM1602_IIC2.RW, LCD2.R/W
  N12: LCM1602_IIC2.E, LCD2.E
  N13: LCM1602_IIC2.D0, LCD2.DB0
  N14: LCM1602_IIC2.D1, LCD2.DB1
  N15: LCM1602_IIC2.D2, LCD2.DB2
  N16: LCM1602_IIC2.D3, LCD2.DB3
  N17: LCM1602_IIC2.D4, LCD2.DB4
  N18: LCM1602_IIC2.D5, LCD2.DB5
  N19: LCM1602_IIC2.D6, LCD2.DB6
  N20: LCM1602_IIC2.D7, LCD2.DB7
  N21: LCM1602_IIC2.A, LCD2.LED+
  N22: LCM1602_IIC2.K, LCD2.LED-

notes:
  Placa Condicionadora do Sensor de Umidade do Solo
  Pinagem
  1 VCC
  2 GND
  3 D0 (sinal digital, 1 se estiver ok a umidade, regulado via potenciometro na plaquinha)
  4 A0 (sinal analógico de umidade)
  Sensor de Umidade do Solo
  Para proteger o circuito de ruído e do efeito antena, colocar em paralelo com o sensor:
  - diodo zenner
  - capacitor eletrolítico de 0,1uF

custom parts:
  LCM1602 IIC: I2C-Module to use a 1602 or 2004 LCD on with the wire.h libory Serial LCD Modul
  DHT11 Humitidy and Temperature Sensor: DHT11 Humidity and Temperature Sensor

// code stored in the sketch: Soil Humidity Sensor.ino
/*Rafael Guimaraes - 16.Set.2016
Código baseado no projeto: http://fritzing.org/projects/soil-humidity-sensor 

*/



#include <Wire.h>
#include <LiquidCrystal_I2C.h>


#define RED 3
#define GREEN 4


LiquidCrystal_I2C lcd(0x27, 16, 2);


void setup()
{
  lcd.begin(16,2);
  lcd.backlight();


  pinMode(RED, OUTPUT);
  pinMode(GREEN, OUTPUT);
}


void loop()
{
  int humidity = map(analogRead(A0), 0, 1023, 100, 0);


  lcd.clear();


  lcd.setCursor(0, 0);
  lcd.print("Humidade : ");
  lcd.print(humidity);
  lcd.print("%");


  lcd.setCursor(0, 1);
  if (humidity > 35) {
    digitalWrite(GREEN, HIGH);
    digitalWrite(RED, LOW);


    lcd.print("Estou bem!");
  }
  else {
    digitalWrite(GREEN, LOW);
    digitalWrite(RED, HIGH);


    lcd.print("Me dê água!");
  }
  delay(1000);
}
